# Fritzing sketch New Piezo (Konfliktkopia för Erik Einebrant 2015-06-09) (saved by Fritzing 0.9.1b)

parts:
  Teensy_3_1 = Teensy 3.1  # not connected
  U6 = mystery part, 14 pins [chip_label=?]
  R56 = Resistor [tolerance=±5% resistance=1M package=THT]
  R57 = Trimmer Potentiometer [maximum_resistance=20k package=THT]
  R58 = Resistor [tolerance=±5% resistance=1k package=THT]
  TRS19 = Audio Jack (TRS) 3.5mm [package="4Ucon 08780 [THT]"]
  TRS20 = Audio Jack (TRS) 3.5mm [package="4Ucon 08780 [THT]"]
  R59 = Resistor [tolerance=±5% resistance=1M package=THT]
  R60 = Resistor [tolerance=±5% resistance=1k package=THT]
  R61 = Resistor [tolerance=±5% resistance=1k package=THT]
  R62 = Trimmer Potentiometer [maximum_resistance=10kΩ package=THT]
  R63 = Trimmer Potentiometer [maximum_resistance=10kΩ package=THT]
  R64 = Resistor [tolerance=±5% resistance=1M package=THT]
  R65 = Trimmer Potentiometer [maximum_resistance=10kΩ package=THT]
  R66 = Resistor [tolerance=±5% resistance=1k package=THT]
  TRS21 = Audio Jack (TRS) 3.5mm [package="4Ucon 08780 [THT]"]
  TRS22 = Audio Jack (TRS) 3.5mm [package="4Ucon 08780 [THT]"]
  R67 = Resistor [tolerance=±5% resistance=1M package=THT]
  U7 = mystery part, 14 pins [chip_label=?]
  R68 = Resistor [tolerance=±5% resistance=1M package=THT]
  R69 = Trimmer Potentiometer [maximum_resistance=20k package=THT]
  R70 = Resistor [tolerance=±5% resistance=1k package=THT]
  TRS23 = Audio Jack (TRS) 3.5mm [package="4Ucon 08780 [THT]"]
  TRS24 = Audio Jack (TRS) 3.5mm [package="4Ucon 08780 [THT]"]
  R71 = Resistor [tolerance=±5% resistance=1M package=THT]
  R72 = Resistor [tolerance=±5% resistance=1k package=THT]
  R73 = Resistor [tolerance=±5% resistance=1k package=THT]
  R74 = Trimmer Potentiometer [maximum_resistance=10kΩ package=THT]
  R75 = Trimmer Potentiometer [maximum_resistance=10kΩ package=THT]
  R76 = Resistor [tolerance=±5% resistance=1M package=THT]
  R77 = Trimmer Potentiometer [maximum_resistance=10kΩ package=THT]
  R78 = Resistor [tolerance=±5% resistance=1k package=THT]
  TRS25 = Audio Jack (TRS) 3.5mm [package="4Ucon 08780 [THT]"]
  TRS26 = Audio Jack (TRS) 3.5mm [package="4Ucon 08780 [THT]"]
  R79 = Resistor [tolerance=±5% resistance=1M package=THT]
  U8 = mystery part, 14 pins [chip_label=?]
  U9 = mystery part, 14 pins [chip_label=?]
  R80 = Resistor [tolerance=±5% resistance=1M package=THT]
  R81 = Resistor [tolerance=±5% resistance=1M package=THT]
  R82 = Trimmer Potentiometer [maximum_resistance=20k package=THT]
  R83 = Trimmer Potentiometer [maximum_resistance=20k package=THT]
  R84 = Resistor [tolerance=±5% resistance=1k package=THT]
  R85 = Resistor [tolerance=±5% resistance=1k package=THT]
  TRS27 = Audio Jack (TRS) 3.5mm [package="4Ucon 08780 [THT]"]
  TRS28 = Audio Jack (TRS) 3.5mm [package="4Ucon 08780 [THT]"]
  TRS29 = Audio Jack (TRS) 3.5mm [package="4Ucon 08780 [THT]"]
  TRS30 = Audio Jack (TRS) 3.5mm [package="4Ucon 08780 [THT]"]
  R86 = Resistor [tolerance=±5% resistance=1M package=THT]
  R87 = Resistor [tolerance=±5% resistance=1M package=THT]
  R88 = Resistor [tolerance=±5% resistance=1k package=THT]
  R89 = Resistor [tolerance=±5% resistance=1k package=THT]
  R90 = Resistor [tolerance=±5% resistance=1k package=THT]
  R91 = Resistor [tolerance=±5% resistance=1k package=THT]
  R92 = Trimmer Potentiometer [maximum_resistance=10kΩ package=THT]
  R93 = Trimmer Potentiometer [maximum_resistance=10kΩ package=THT]
  R94 = Trimmer Potentiometer [maximum_resistance=10kΩ package=THT]
  R95 = Trimmer Potentiometer [maximum_resistance=10kΩ package=THT]
  R96 = Resistor [tolerance=±5% resistance=1M package=THT]
  R97 = Resistor [tolerance=±5% resistance=1M package=THT]
  R98 = Trimmer Potentiometer [maximum_resistance=10kΩ package=THT]
  R99 = Trimmer Potentiometer [maximum_resistance=10kΩ package=THT]
  R100 = Resistor [tolerance=±5% resistance=1k package=THT]
  R101 = Resistor [tolerance=±5% resistance=1k package=THT]
  TRS31 = Audio Jack (TRS) 3.5mm [package="4Ucon 08780 [THT]"]
  TRS32 = Audio Jack (TRS) 3.5mm [package="4Ucon 08780 [THT]"]
  TRS33 = Audio Jack (TRS) 3.5mm [package="4Ucon 08780 [THT]"]
  TRS34 = Audio Jack (TRS) 3.5mm [package="4Ucon 08780 [THT]"]
  R102 = Resistor [tolerance=±5% resistance=1M package=THT]
  R103 = Resistor [tolerance=±5% resistance=1M package=THT]

nets:
  N1: U6.pin1, R63.wiper
  N2: U6.pin2, R60.Pin_0
  N3: U6.pin3, TRS22.Tip, R67.Pin_0, R67.Pin_1
  N4: U6.pin5, R64.Pin_1, TRS21.Ring
  N5: U6.pin6, R65.wiper, R66.Pin_1
  N6: U6.pin8, R62.wiper
  N7: U6.pin9, U6.pin10, TRS20.Tip, R59.Pin_0, R61.Pin_0
  N8: U6.pin11, R58.Pin_1, R61.Pin_1
  N9: U6.pin12, R56.Pin_0, R56.Pin_1, TRS19.Ring, R59.Pin_1
  N10: U6.pin13, R57.leg2, R58.Pin_0
  N11: U6.pin14, R57.wiper
  N12: TRS19.Sleeve, TRS20.Sleeve, TRS23.Sleeve, TRS24.Sleeve, TRS27.Sleeve, TRS28.Sleeve, TRS29.Sleeve, TRS30.Sleeve
  N13: R60.Pin_1, R64.Pin_0, R66.Pin_0
  N14: TRS21.Sleeve, TRS22.Sleeve, TRS25.Sleeve, TRS26.Sleeve, TRS31.Sleeve, TRS32.Sleeve, TRS33.Sleeve, TRS34.Sleeve
  N15: U7.pin1, R75.wiper
  N16: U7.pin2, R72.Pin_0
  N17: U7.pin3, TRS26.Tip, R79.Pin_0, R79.Pin_1
  N18: U7.pin5, R76.Pin_1, TRS25.Ring
  N19: U7.pin6, R77.wiper, R78.Pin_1
  N20: U7.pin8, R74.wiper
  N21: U7.pin9, U7.pin10, TRS24.Tip, R71.Pin_0, R73.Pin_0
  N22: U7.pin11, R70.Pin_1, R73.Pin_1
  N23: U7.pin12, R68.Pin_0, R68.Pin_1, TRS23.Ring, R71.Pin_1
  N24: U7.pin13, R69.leg2, R70.Pin_0
  N25: U7.pin14, R69.wiper
  N26: R72.Pin_1, R76.Pin_0, R78.Pin_0
  N27: U8.pin1, R95.wiper
  N28: U8.pin2, R88.Pin_0
  N29: U8.pin3, TRS34.Tip, R102.Pin_0, R102.Pin_1
  N30: U8.pin5, R96.Pin_1, TRS31.Ring
  N31: U8.pin6, R98.wiper, R100.Pin_1
  N32: U8.pin8, R92.wiper
  N33: U8.pin9, U8.pin10, TRS29.Tip, R86.Pin_0, R90.Pin_0
  N34: U8.pin11, R84.Pin_1, R90.Pin_1
  N35: U8.pin12, R81.Pin_0, R81.Pin_1, TRS27.Ring, R86.Pin_1
  N36: U8.pin13, R83.leg2, R84.Pin_0
  N37: U8.pin14, R83.wiper
  N38: U9.pin1, R94.wiper
  N39: U9.pin2, R89.Pin_0
  N40: U9.pin3, TRS33.Tip, R103.Pin_0, R103.Pin_1
  N41: U9.pin5, R97.Pin_1, TRS32.Ring
  N42: U9.pin6, R99.wiper, R101.Pin_1
  N43: U9.pin8, R93.wiper
  N44: U9.pin9, U9.pin10, TRS30.Tip, R87.Pin_0, R91.Pin_0
  N45: U9.pin11, R85.Pin_1, R91.Pin_1
  N46: U9.pin12, R80.Pin_0, R80.Pin_1, TRS28.Ring, R87.Pin_1
  N47: U9.pin13, R82.leg2, R85.Pin_0
  N48: U9.pin14, R82.wiper
  N49: R88.Pin_1, R96.Pin_0, R100.Pin_0
  N50: R89.Pin_1, R97.Pin_0, R101.Pin_0
